# Fritzing sketch hm10-ledBlink (saved by Fritzing 0.9.2b)
breadboards: 1

parts:
  Componente1 = Arduino Uno (Rev3)
  Componente2 = Bluetooth HM-10
  R1 = Resistor [tolerance=±5% resistance=220 package=THT]
  LED1 = LED - 5mm [color="Red (633nm)" package="5 mm [THT]"]

nets:
  N1: Componente1.D13/SCK, R1.Pin_1
  N2: Componente1.D0/RX, Componente2.TXD
  N3: Componente1.D1/TX, Componente2.RXD
  3V3: Componente1.3V3, Componente2.VCC
  GND: Componente1.GND, Componente2.GND, LED1.cathode
  N4: R1.Pin_0, LED1.anode

// code stored in the sketch: hm10-ledBlink.ino
/****************************************/
#define ledPin 13  // //pin 13 built-in LED light
int val;
void setup()
{
  Serial.begin(9600);
  pinMode(ledPin, OUTPUT);
}
void loop()
{
  if(Serial.available()) //
  {
    val = Serial.read();
    if(val =='A')  //if comes a 'A',LED on control board will blink
    {
      digitalWrite(ledPin, HIGH);
      Serial.println("ligado");  //print on Serial debugging assistant on computer
    }
    else if(val == 'B'){
      digitalWrite(ledPin, LOW);
      Serial.println("desligado");  //print on Serial debugging assistant on computer
    }
  }
}
/****************************************/
